// Logisim project fp_logic.circ as structural Verilog: 3 circuits, main circuit fp_mult
module fp_mult (
  input  [31:0] in1,
  input  [31:0] in2,
  output [31:0] out
);

  wire [31:0] multiplier_1_cout, multiplier_1_out, shifter_1_out, shifter_2_out;

  Multiplier #(.width(32)) multiplier_1 (
    .a(in1), .b(in2), .out(multiplier_1_out), .cout(multiplier_1_cout));  // open: cin
  Shifter #(.width(32), .shift("lr")) shifter_1 (.in(multiplier_1_out), .\dist (5'b10000), .out(shifter_1_out));
  Shifter #(.width(32)) shifter_2 (.in(multiplier_1_cout), .\dist (5'b10000), .out(shifter_2_out));
  Adder #(.width(32)) adder_1 (.a(shifter_1_out), .b(shifter_2_out), .out(out));  // open: cin, cout

  // Notes on the sheet:
  //   in1: pull=down
  //   in2: pull=down
  //   out: pull=down
  //   for now ignore
  //   TODO?: take care of carry (in both case the carry is out of 32bit bounds
endmodule

module fp_div (
  input  [31:0] in1,
  input  [31:0] in2,
  output [31:0] out
);

  wire [31:0] adder_1_out, divider_1_out, divider_1_rem, divider_2_out, fp_abs_1_abs, fp_abs_2_abs,
       shifter_1_out, shifter_2_out;
  wire [31:31] xor_1_out;

  xor xor_1 (xor_1_out[31], in2[31], in1[31]);
  fp_abs fp_abs_1 (.in(in1), .abs(fp_abs_1_abs));
  fp_abs fp_abs_2 (.in(in2), .abs(fp_abs_2_abs));
  Divider #(.width(32)) divider_1 (
    .a(fp_abs_1_abs), .b(fp_abs_2_abs), .out(divider_1_out), .rem(divider_1_rem));  // open: upper
  Shifter #(.width(32), .shift("lr")) shifter_1 (.in(fp_abs_2_abs), .\dist (5'b10000), .out(shifter_1_out));
  Shifter #(.width(32)) shifter_2 (.in(divider_1_out), .\dist (5'b10000), .out(shifter_2_out));
  Adder #(.width(32)) adder_1 (.a(shifter_2_out), .b(divider_2_out), .out(adder_1_out));  // open: cin, cout
  Divider #(.width(32)) divider_2 (.a(divider_1_rem), .b(shifter_1_out), .out(divider_2_out));  // open: upper, rem
  assign out = {xor_1_out[31], {31{1'b0}}} | adder_1_out;  // OR_Gate or_1, 32 bits wide

  // Notes on the sheet:
  //   out: pull=down
  //   in2: pull=down
  //   in1: pull=down
endmodule

module fp_abs (
  input  [31:0] in,
  output [31:0] abs
);

  wire [31:0] negator_1_out;

  Negator #(.width(32)) negator_1 (.in(in), .out(negator_1_out));
  Multiplexer #(.width(32), .enable("false")) multiplexer_1 (.in0(in), .in1(negator_1_out), .out(abs), .sel(in[31]));

  // Notes on the sheet:
  //   abs: pull=down
  //   in: pull=down
endmodule
